// Logisim project TP Noté RICHARD Corentin .circ as structural Verilog: 13 circuits, main circuit main
module main (
  input  Rst
);

  wire A_we, ALU_we, aluPC, BImm, BMem, BReg, clock_1_out, clock_2_out, clock_3_out, clock_5_out, Extend,
       Extended, Fetch, Fetch_q, Fi, RI_we, Write, ZNCV_we;
  wire [1:0] Extra;
  wire [2:0] OpSpe;
  wire [3:0] Ad_n, As_n, B_n, Op, ZNCV;
  wire [4:0] Format;
  wire [15:0] address_incrementer_1_incrementer_bus, address_register_1_a15_0,
       address_register_1_incrementer_bus_source, alu_1_s, BBus, controlled_buffer_1_out, Imm, R1_q,
       ram_1_dout, register_bank_1_a, register_bank_1_pc_bus, Wdr;

  // Probe on alu_1_s
  ALU alu_1 (
    .ZNCV(ZNCV), .S(alu_1_s), .ZNCV_we(ZNCV_we), .Op_Spe(OpSpe), .B(controlled_buffer_1_out),
    .A(register_bank_1_a), .Op(Op));
  // Probe on register_bank_1_a
  Address_incrementer address_incrementer_1 (
    .Incrementer_bus(address_incrementer_1_incrementer_bus),
    .Incrementer_bus_source(address_register_1_incrementer_bus_source));
  // Probe on BBus
  assign controlled_buffer_1_out = BReg ? BBus : 16'bz;  // Controlled_Buffer controlled_buffer_1
  // Probe on controlled_buffer_1_out
  Address_register address_register_1 (
    .Incrementer_bus_source(address_register_1_incrementer_bus_source), .A15_0(address_register_1_a15_0),
    .Incrementer_bus(address_incrementer_1_incrementer_bus), .AR_we(ALU_we), .ALU_bus(alu_1_s), .Rst(Rst),
    .PC_bus(register_bank_1_pc_bus), .aluPC(aluPC));  // open: Incbus_we
  Register_bank register_bank_1 (
    .A(register_bank_1_a), .B(BBus), .PC_bus(register_bank_1_pc_bus), .Ad_we(A_we), .Rst(Rst),
    .INC_bus(address_incrementer_1_incrementer_bus), .ALU_bus(alu_1_s), .Ad_n(Ad_n), .Bs_n(B_n), .As_n(As_n));
  // Probe on address_register_1_a15_0
  Clock clock_1 (.out(clock_1_out));
  assign controlled_buffer_1_out = BMem ? ram_1_dout : 16'bz;  // Controlled_Buffer controlled_buffer_2
  Write_data_register write_data_register_1 (.D(Wdr), .B(BBus));
  assign controlled_buffer_1_out = BImm ? Imm : 16'bz;  // Controlled_Buffer controlled_buffer_3
  RAM #(.addrWidth(16), .dataWidth(16), .enables("line"), .\type ("nonvolatile")) ram_1 (
    .addr(address_register_1_a15_0), .we(Write), .clk(clock_1_out), .din(Wdr), .dout(ram_1_dout));
  // Probe on ram_1_dout
  // Probe on ram_1_dout
  Register #(.width(1)) u_Fetch (.D(Fetch), .en(Fi), .clk(clock_2_out), .Q(Fetch_q), .clr(Rst));
  Clock clock_2 (.out(clock_2_out));
  Register #(.width(16)) R1 (.D(ram_1_dout), .en(RI_we), .clk(clock_3_out), .Q(R1_q), .clr(Rst));
  Clock clock_3 (.out(clock_3_out));
  Clock clock_4 ();  // open: out
  not not_1 (Fetch, Fetch_q);
  Register #(.width(1)) u_Extend (.D(Extend), .en(1'b1), .clk(clock_5_out), .Q(Extended), .clr(Rst));
  Clock clock_5 (.out(clock_5_out));
  // Probe on Format
  Instr_Format instr_format_1 (.Instr(R1_q[15:8]), .Format(Format));
  Sequenceur sequenceur_1 (
    .Fetch(Fetch), .Format(Format), .Extra(Extra), .Extended(Extended), .Extend(Extend), .Fi(Fi),
    .RI_we(RI_we), .Breg(BReg), .BMem(BMem), .BImm(BImm), .A_we(A_we), .OpSpe(OpSpe), .Write(Write),
    .ZNCV_we(ZNCV_we), .aluPC(aluPC), .ALU_we(ALU_we));
  Instr_Rn instr_rn_1 (.Instr(R1_q), .Format(Format), .Fetch(Fetch), .Ad_n(Ad_n), .As_n(As_n), .B_n(B_n));
  Instr_Imm instr_imm_1 (.Instr(R1_q), .Fetch(Fetch), .Format(Format), .Imm(Imm));
  Instr_Extra instr_extra_1 (.Instr(R1_q), .Format(Format), .Extra(Extra));  // open: ZNCV
  Instr_op instr_op_1 (.Instr(R1_q), .Format(Format), .Op(Op));
  // Probe on Ad_n
  // Probe on As_n
  // Probe on B_n
  // Probe on Imm
  // Probe on Extra
  // Probe on Op
endmodule

module Address_register (
  input  [15:0] ALU_bus,
  input  AR_we,
  input  [15:0] PC_bus,
  input  aluPC,
  input  Rst,
  input  [15:0] Incrementer_bus,
  input  Incbus_we,
  output [15:0] A15_0,
  output [15:0] Incrementer_bus_source
);

  wire clock_1_out;
  wire [15:0] multiplexer_1_out, register_1_q;

  Clock clock_1 (.out(clock_1_out));
  Register #(.width(16)) register_1 (.D(ALU_bus), .en(AR_we), .clk(clock_1_out), .Q(register_1_q), .clr(Rst));
  Multiplexer #(.width(16)) multiplexer_1 (.in0(register_1_q), .in1(PC_bus), .out(multiplexer_1_out), .sel(aluPC));
  Shifter #(.shift("lr"), .width(16)) shifter_1 (.in(multiplexer_1_out), .\dist (4'b0001), .out(A15_0));
endmodule

module Register_bank (
  input  [15:0] INC_bus,
  input  [15:0] ALU_bus,
  input  Rst,
  input  Ad_we,
  input  [3:0] Ad_n,
  input  [3:0] As_n,
  input  [3:0] Bs_n,
  output [15:0] A,
  output [15:0] B,
  output [15:0] PC_bus
);

  wire clock_1_out, clock_2_out, clock_3_out, clock_4_out, clock_5_out, clock_6_out, demultiplexer_1_out0,
       demultiplexer_1_out1, demultiplexer_1_out2, demultiplexer_1_out3, demultiplexer_1_out4,
       demultiplexer_1_out15;
  wire [15:0] R0_q, R1_q, R2_q, R3_q, R4_q;

  Demultiplexer #(.select(4)) demultiplexer_1 (
    .out0(demultiplexer_1_out0), .out1(demultiplexer_1_out1), .out2(demultiplexer_1_out2),
    .out3(demultiplexer_1_out3), .out4(demultiplexer_1_out4), .out15(demultiplexer_1_out15), .in(Ad_we),
    .sel(Ad_n));  // open: out5, out6, out7, out8, out9, out10, out11, out12, out13, out14
  Register #(.width(16)) R0 (.D(ALU_bus), .en(demultiplexer_1_out0), .clk(clock_1_out), .Q(R0_q), .clr(Rst));
  Clock clock_1 (.out(clock_1_out));
  Register #(.width(16)) R1 (.D(ALU_bus), .en(demultiplexer_1_out1), .clk(clock_2_out), .Q(R1_q), .clr(Rst));
  Clock clock_2 (.out(clock_2_out));
  Register #(.width(16)) R2 (.D(ALU_bus), .en(demultiplexer_1_out2), .clk(clock_3_out), .Q(R2_q), .clr(Rst));
  Clock clock_3 (.out(clock_3_out));
  Register #(.width(16)) R3 (.D(ALU_bus), .en(demultiplexer_1_out3), .clk(clock_4_out), .Q(R3_q), .clr(Rst));
  Clock clock_4 (.out(clock_4_out));
  Register #(.width(16)) R4 (.D(ALU_bus), .en(demultiplexer_1_out4), .clk(clock_5_out), .Q(R4_q), .clr(Rst));
  Clock clock_5 (.out(clock_5_out));
  Register #(.width(16)) R15 (.D(ALU_bus), .en(demultiplexer_1_out15), .clk(clock_6_out), .Q(PC_bus), .clr(Rst));
  Clock clock_6 (.out(clock_6_out));
  Multiplexer #(.select(4), .width(16)) multiplexer_1 (
    .in0(R0_q), .in1(R1_q), .in2(R2_q), .in3(R3_q), .in4(R4_q), .in15(PC_bus), .out(A), .sel(As_n));  // open: in5, in6, in7, in8, in9, in10, in11, in12, in13, in14
  Multiplexer #(.select(4), .width(16)) multiplexer_2 (
    .in0(R0_q), .in1(R1_q), .in2(R2_q), .in3(R3_q), .in4(R4_q), .in15(PC_bus), .out(B), .sel(Bs_n));  // open: in5, in6, in7, in8, in9, in10, in11, in12, in13, in14
endmodule

module ALU (
  input  [3:0] Op,
  input  [15:0] B,
  input  [15:0] A,
  input  ZNCV_we,
  input  [2:0] Op_Spe,
  output [3:0] ZNCV,
  output [15:0] S
);

  wire clock_1_out, nor_1_out;
  wire [15:0] adder_1_out, multiplexer_1_out, or_1_out, subtractor_1_out, subtractor_2_out;

  Subtractor #(.width(16)) subtractor_1 (.a(A), .b(B), .out(subtractor_1_out));  // open: bin, bout
  assign or_1_out = A | B;  // OR_Gate or_1, 16 bits wide
  Adder #(.width(16)) adder_1 (.a(A), .b(B), .out(adder_1_out));  // open: cin, cout
  Subtractor #(.width(16)) subtractor_2 (.a(A), .b(B), .out(subtractor_2_out));  // open: bin, bout
  Multiplexer #(.select(4), .width(16)) multiplexer_1 (
    .in10(subtractor_1_out), .in12(or_1_out), .out(multiplexer_1_out), .sel(Op));  // open: in0, in1, in2, in3, in4, in5, in6, in7, in8, in9, in11, in13, in14, in15
  Multiplexer #(.select(3), .width(16)) multiplexer_2 (
    .in0(multiplexer_1_out), .in1(B), .in2(adder_1_out), .in3(subtractor_2_out), .out(S), .sel(Op_Spe));  // open: in4, in5, in6, in7
  nor nor_1 (nor_1_out, S[0], S[1], S[2], S[3], S[4], S[5], S[6], S[7], S[8], S[9], S[10], S[11], S[12], S[13], S[14], S[15]);
  Clock clock_1 (.out(clock_1_out));
  Register #(.width(1)) Z (.D(nor_1_out), .en(ZNCV_we), .clk(clock_1_out), .Q(ZNCV[0]));  // open: clr
  Register #(.width(1)) N (.D(S[15]), .en(ZNCV_we), .clk(clock_1_out), .Q(ZNCV[1]));  // open: clr
  Register #(.width(1)) register_1 (.en(ZNCV_we), .clk(clock_1_out), .Q(ZNCV[2]));  // open: D, clr
  Register #(.width(1)) register_2 (.en(ZNCV_we), .clk(clock_1_out), .Q(ZNCV[3]));  // open: D, clr
endmodule

module Write_data_register (
  input  [15:0] B,
  output [15:0] D
);


  assign D = B;
endmodule

module Address_incrementer (
  input  [15:0] Incrementer_bus_source,
  output [15:0] Incrementer_bus
);
endmodule

module Instr_Format (
  input  [7:0] Instr,
  output [4:0] Format
);

  wire and_1_out, and_2_out, and_4_out, and_5_out, and_6_out, and_7_out, and_8_out, and_9_out, and_10_out,
       and_11_out, and_12_out, and_13_out, and_14_out, and_15_out, not_1_out, not_2_out, not_3_out,
       not_4_out, not_5_out;

  not not_1 (not_1_out, Instr[7]);
  not not_2 (not_2_out, Instr[6]);
  not not_3 (not_3_out, Instr[5]);
  not not_4 (not_4_out, Instr[4]);
  not not_5 (not_5_out, Instr[3]);
  and and_1 (and_1_out, Instr[7], Instr[6], not_3_out, Instr[4]);
  or or_1 (Format[4], and_1_out, and_2_out);
  and and_2 (and_2_out, Instr[7], Instr[6], Instr[5], not_4_out, not_5_out);
  and and_3 (Format[3], not_1_out, Instr[6], Instr[5]);
  and and_4 (and_4_out, not_1_out, Instr[6], not_3_out);
  and and_5 (and_5_out, Instr[6], not_3_out, not_4_out);
  and and_6 (and_6_out, Instr[7], Instr[6], not_4_out, Instr[3]);
  and and_7 (and_7_out, Instr[7], Instr[6], Instr[5], Instr[4]);
  and and_8 (and_8_out, not_3_out, not_4_out, Instr[2]);
  and and_9 (and_9_out, not_3_out, not_4_out, Instr[3]);
  and and_10 (and_10_out, not_1_out, not_3_out, Instr[4]);
  and and_11 (and_11_out, Instr[7], Instr[5]);
  and and_12 (and_12_out, not_1_out, Instr[5]);
  and and_13 (and_13_out, not_2_out, Instr[5]);
  and and_14 (and_14_out, Instr[5], Instr[3]);
  and and_15 (and_15_out, Instr[5], Instr[4]);
  or or_2 (Format[2], and_4_out, and_5_out, and_6_out, and_7_out);
  or or_3 (Format[1], not_2_out, and_8_out, and_9_out, and_10_out, and_11_out);
  or or_4 (Format[0], and_12_out, and_13_out, and_14_out, and_15_out);
endmodule

module Instr_Rn (
  input  [15:0] Instr,
  input  [4:0] Format,
  input  Fetch,
  output [3:0] Ad_n,
  output [3:0] As_n,
  output [3:0] B_n
);

  wire [3:0] bit_extender_1_out, bit_extender_2_out, bit_extender_3_out, bit_extender_4_out,
       bit_extender_5_out, bit_extender_6_out, bit_extender_7_out, bit_extender_8_out, bit_extender_9_out,
       bit_extender_10_out, multiplexer_1_out, multiplexer_2_out;

  assign bit_extender_1_out = {{1{1'b0}}, Instr[5:3]};  // Bit_Extender bit_extender_1
  assign bit_extender_2_out = {{1{1'b0}}, Instr[10:8]};  // Bit_Extender bit_extender_2
  assign bit_extender_3_out = {{1{1'b0}}, Instr[2:0]};  // Bit_Extender bit_extender_3
  assign bit_extender_4_out = {{1{1'b0}}, Instr[5:3]};  // Bit_Extender bit_extender_4
  assign bit_extender_5_out = {{1{1'b0}}, Instr[8:6]};  // Bit_Extender bit_extender_5
  assign bit_extender_6_out = {{1{1'b0}}, Instr[5:3]};  // Bit_Extender bit_extender_6
  assign bit_extender_7_out = {{1{1'b0}}, Instr[2:0]};  // Bit_Extender bit_extender_7
  assign bit_extender_8_out = {{1{1'b0}}, Instr[2:0]};  // Bit_Extender bit_extender_8
  assign bit_extender_9_out = {{1{1'b0}}, Instr[10:8]};  // Bit_Extender bit_extender_9
  assign bit_extender_10_out = {{1{1'b0}}, Instr[2:0]};  // Bit_Extender bit_extender_10
  Multiplexer #(.select(5), .width(4)) multiplexer_1 (
    .in2(bit_extender_8_out), .in3(bit_extender_9_out), .in4(bit_extender_10_out), .in9(bit_extender_10_out),
    .in16(4'b1111), .in18(4'b1111), .out(multiplexer_1_out), .sel(Format));  // open: in0, in1, in5, in6, in7, in8, in10, in11, in12, in13, in14, in15, in17, in19, in20, in21, in22, in23, in24, in25, in26, in27, in28, in29, in30, in31
  Multiplexer #(.select(5), .width(4)) multiplexer_2 (
    .in2(bit_extender_1_out), .in3(bit_extender_2_out), .in4(bit_extender_3_out), .in9(bit_extender_4_out),
    .in16(4'b1111), .in18(4'b1111), .out(multiplexer_2_out), .sel(Format));  // open: in0, in1, in5, in6, in7, in8, in10, in11, in12, in13, in14, in15, in17, in19, in20, in21, in22, in23, in24, in25, in26, in27, in28, in29, in30, in31
  Multiplexer #(.select(5), .width(4)) multiplexer_3 (
    .in2(bit_extender_5_out), .in4(bit_extender_6_out), .in9(bit_extender_7_out), .out(B_n), .sel(Format));  // open: in0, in1, in3, in5, in6, in7, in8, in10, in11, in12, in13, in14, in15, in16, in17, in18, in19, in20, in21, in22, in23, in24, in25, in26, in27, in28, in29, in30, in31
  Multiplexer #(.width(4)) multiplexer_4 (.in0(multiplexer_1_out), .in1(4'b1111), .out(Ad_n), .sel(Fetch));
  Multiplexer #(.width(4)) multiplexer_5 (.in0(multiplexer_2_out), .in1(4'b1111), .out(As_n), .sel(Fetch));
endmodule

module Instr_Imm (
  input  [15:0] Instr,
  input  Fetch,
  input  [4:0] Format,
  output [15:0] Imm
);

  wire [15:0] adder_1_out, bit_extender_1_out, bit_extender_2_out, bit_extender_3_out, bit_extender_4_out,
       bit_extender_5_out, multiplexer_1_out, shifter_1_out, shifter_2_out, shifter_3_out;

  assign bit_extender_1_out = {{8{1'b0}}, Instr[7:0]};  // Bit_Extender bit_extender_1
  assign bit_extender_2_out = {{5{1'b0}}, Instr[10:0]};  // Bit_Extender bit_extender_2
  assign bit_extender_3_out = {{13{1'b0}}, Instr[8:6]};  // Bit_Extender bit_extender_3
  assign bit_extender_4_out = {{8{1'b0}}, Instr[7:0]};  // Bit_Extender bit_extender_4
  assign bit_extender_5_out = {{11{1'b0}}, Instr[10:6]};  // Bit_Extender bit_extender_5
  Shifter #(.width(16)) shifter_1 (.in(bit_extender_5_out), .\dist (4'b0010), .out(shifter_1_out));
  Shifter #(.width(16)) shifter_2 (.in(bit_extender_1_out), .\dist (4'b0001), .out(shifter_2_out));
  Shifter #(.width(16)) shifter_3 (.in(bit_extender_2_out), .\dist (4'b0001), .out(shifter_3_out));
  Multiplexer #(.select(5), .width(16)) multiplexer_1 (
    .in2(bit_extender_3_out), .in3(bit_extender_4_out), .in9(shifter_1_out), .in16(shifter_2_out),
    .in18(adder_1_out), .out(multiplexer_1_out), .sel(Format));  // open: in0, in1, in4, in5, in6, in7, in8, in10, in11, in12, in13, in14, in15, in17, in19, in20, in21, in22, in23, in24, in25, in26, in27, in28, in29, in30, in31
  Adder #(.width(16)) adder_1 (.a(shifter_3_out), .b(16'h2), .out(adder_1_out));  // open: cin, cout
  Multiplexer #(.width(16)) multiplexer_2 (.in0(multiplexer_1_out), .in1(16'h2), .out(Imm), .sel(Fetch));
endmodule

module Sequenceur (
  input  Fetch,
  input  [4:0] Format,
  input  [1:0] Extra,
  input  Extended,
  output Extend,
  output Fi,
  output RI_we,
  output Breg,
  output BMem,
  output BImm,
  output A_we,
  output [2:0] OpSpe,
  output Write,
  output ZNCV_we,
  output aluPC,
  output ALU_we
);

  wire and_2_out, and_3_out, and_4_out, and_5_out, and_6_out, and_7_out, and_8_out, and_9_out, and_11_out,
       and_12_out, and_13_out, and_14_out, and_15_out, and_16_out, and_17_out, and_18_out, and_19_out,
       and_20_out, and_21_out, and_22_out, and_23_out, and_24_out, and_25_out, and_26_out, and_27_out,
       and_28_out, and_29_out, and_30_out, and_31_out, and_32_out, and_33_out, and_34_out, and_35_out,
       and_36_out, not_1_out, not_2_out, not_3_out, not_4_out, not_5_out, not_6_out, not_7_out, not_8_out,
       not_9_out;

  not not_1 (not_1_out, Fetch);
  not not_2 (not_2_out, Format[4]);
  not not_3 (not_3_out, Format[3]);
  not not_4 (not_4_out, Format[2]);
  not not_5 (not_5_out, Format[1]);
  not not_6 (not_6_out, Format[0]);
  not not_7 (not_7_out, Extra[1]);
  not not_8 (not_8_out, Extra[0]);
  not not_9 (not_9_out, Extended);
  and and_1 (Extend, not_1_out, not_2_out, Format[3], not_4_out, not_5_out, Format[0], not_9_out);
  or or_1 (Fi, not_3_out, not_6_out, Extended, Format[1], Format[2], Format[4], Fetch);
  and and_2 (and_2_out, not_1_out, not_2_out, not_3_out, not_5_out);
  and and_3 (and_3_out, not_1_out, not_2_out, not_6_out, not_7_out);
  and and_4 (and_4_out, not_1_out, not_5_out, not_8_out, Extended);
  and and_5 (and_5_out, not_1_out, Format[2]);
  and and_6 (and_6_out, not_1_out, Format[3], not_6_out);
  and and_7 (and_7_out, not_1_out, Format[3], Format[1]);
  and and_8 (and_8_out, not_1_out, Format[4], not_5_out, not_8_out);
  and and_9 (and_9_out, not_1_out, Format[4], Format[0]);
  and and_10 (BMem, not_1_out, not_2_out, Format[3], not_4_out, not_5_out, Format[0], Extra[0], Extended);
  and and_11 (and_11_out, not_3_out, not_4_out, Format[1], not_6_out, Extra[1]);
  and and_12 (and_12_out, not_2_out, not_3_out, not_4_out, Format[1], Format[0]);
  and and_13 (and_13_out, not_2_out, Format[3], not_4_out, not_5_out, Format[0], not_9_out);
  and and_14 (and_14_out, Format[4], not_3_out, not_4_out, not_6_out, Extra[0]);
  and and_15 (and_15_out, Format[4], not_3_out, not_4_out, Format[1], not_6_out);
  and and_16 (and_16_out, not_2_out, not_3_out, not_8_out);
  and and_17 (and_17_out, not_6_out, Extra[0]);
  and and_18 (and_18_out, not_3_out, not_5_out, Format[0]);
  and and_19 (and_19_out, Format[1], Extra[1]);
  and and_20 (and_20_out, Format[3], not_6_out);
  and and_21 (and_21_out, Format[3], Extra[0], Extended);
  and and_22 (and_22_out, Format[3], Format[1]);
  and and_23 (and_23_out, Format[4], Format[0]);
  and and_24 (and_24_out, Format[4], Format[1]);
  and and_25 (and_25_out, not_3_out, not_4_out, not_5_out);
  and and_26 (and_26_out, not_4_out, not_6_out);
  and and_27 (and_27_out, Format[1], not_6_out);
  and and_28 (and_28_out, Format[1], Extra[0]);
  and and_29 (and_29_out, Format[1], Extra[1]);
  and and_30 (and_30_out, Format[2], Format[0]);
  and and_31 (and_31_out, Format[3], not_6_out);
  and and_32 (and_32_out, Format[3], not_9_out);
  and and_33 (and_33_out, Format[3], Format[1]);
  and and_34 (and_34_out, not_1_out, not_2_out, not_3_out, not_4_out, Format[1], Extra[0]);
  and and_35 (and_35_out, not_1_out, not_2_out, not_3_out, not_4_out, Format[1], Format[0], not_7_out);
  and and_36 (and_36_out, not_1_out, not_2_out, Format[3], not_4_out, not_5_out, Format[0], Extended);
  and and_37 (Write, not_1_out, not_2_out, Format[3], not_4_out, not_5_out, Format[0], not_8_out, Extended);
  and and_38 (ZNCV_we, not_1_out, not_2_out);
  or or_2 (aluPC, not_3_out, not_6_out, not_9_out, Format[1], Format[2], Format[4], Fetch);
  and and_39 (ALU_we, not_1_out, not_2_out, Format[3], not_4_out, not_5_out, Format[0], not_9_out);
  or or_3 (Breg, and_2_out, and_3_out, and_4_out, and_5_out, and_6_out, and_7_out, and_8_out, and_9_out);
  or or_4 (BImm, and_11_out, and_12_out, and_13_out, and_14_out, and_15_out, Fetch);
  or or_5 (A_we, and_16_out, and_17_out, and_18_out, and_19_out, Format[2], and_20_out, and_21_out, and_22_out, and_23_out, and_24_out, Fetch);
  or or_6 (OpSpe[1], and_25_out, and_26_out, and_27_out, and_28_out, and_29_out, and_30_out, and_31_out, and_32_out, and_33_out, Format[4], Fetch);
  or or_7 (OpSpe[0], and_34_out, and_35_out, and_36_out);

  assign OpSpe[2] = 1'b0;
  assign RI_we = Fetch;
endmodule

module Instr_Extra (
  input  [15:0] Instr,
  input  [4:0] Format,
  input  [3:0] ZNCV,
  output [1:0] Extra
);

  wire instr_cond_1_extra;
  wire [1:0] Instr16, multiplexer_1_out;

  Multiplexer #(.select(4), .width(2)) multiplexer_1 (
    .in0(2'b00), .in1(2'b00), .in2(2'b00), .in3(2'b00), .in4(2'b00), .in5(2'b00), .in6(2'b00), .in7(2'b00),
    .in8(2'b01), .in9(2'b00), .in10(2'b01), .in11(2'b01), .in12(2'b00), .in13(2'b00), .in14(2'b00),
    .in15(2'b00), .out(multiplexer_1_out), .sel(Instr[9:6]));
  Multiplexer #(.select(5), .width(2)) multiplexer_2 (
    .in2(Instr[10:9]), .in3(Instr[12:11]), .in4(multiplexer_1_out), .in9(Instr[12:11]), .in16(Instr16),
    .out(Extra), .sel(Format));  // open: in0, in1, in5, in6, in7, in8, in10, in11, in12, in13, in14, in15, in17, in18, in19, in20, in21, in22, in23, in24, in25, in26, in27, in28, in29, in30, in31
  Instr_Cond instr_cond_1 (.ZNCV(ZNCV), .Cond(Instr[11:8]), .Extra(instr_cond_1_extra));
  assign Instr16 = {{1{1'b0}}, instr_cond_1_extra};  // Bit_Extender bit_extender_1
endmodule

module Instr_op (
  input  [15:0] Instr,
  input  [4:0] Format,
  output [3:0] Op
);

  Multiplexer #(.select(5), .width(4)) multiplexer_1 (
    .in4(Instr[9:6]), .out(Op), .sel(Format));  // open: in0, in1, in2, in3, in5, in6, in7, in8, in9, in10, in11, in12, in13, in14, in15, in16, in17, in18, in19, in20, in21, in22, in23, in24, in25, in26, in27, in28, in29, in30, in31
endmodule

module Instr_Cond (
  input  [3:0] ZNCV,
  input  [3:0] Cond,
  output Extra
);

  wire and_1_out, and_2_out, and_3_out, and_4_out, and_5_out, and_6_out, and_7_out, and_8_out, and_9_out,
       and_10_out, and_11_out, and_12_out, and_13_out, and_14_out, and_15_out, and_16_out, and_17_out,
       and_18_out, and_19_out, and_20_out, not_1_out, not_2_out, not_3_out, not_4_out, not_5_out, not_6_out,
       not_7_out, not_8_out;

  not not_1 (not_1_out, ZNCV[3]);
  not not_2 (not_2_out, ZNCV[2]);
  not not_3 (not_3_out, ZNCV[1]);
  not not_4 (not_4_out, ZNCV[0]);
  not not_5 (not_5_out, Cond[3]);
  not not_6 (not_6_out, Cond[2]);
  not not_7 (not_7_out, Cond[1]);
  not not_8 (not_8_out, Cond[0]);
  and and_1 (and_1_out, not_1_out, not_2_out, not_5_out, not_7_out, Cond[0]);
  and and_2 (and_2_out, not_1_out, not_5_out, not_6_out, not_7_out, Cond[0]);
  and and_3 (and_3_out, not_3_out, not_5_out, not_6_out, Cond[1], Cond[0]);
  and and_4 (and_4_out, not_2_out, not_5_out, Cond[2], not_7_out, Cond[0]);
  and and_5 (and_5_out, not_4_out, Cond[2], Cond[1], Cond[0]);
  and and_6 (and_6_out, not_2_out, not_4_out, Cond[3], Cond[1], not_8_out);
  and and_7 (and_7_out, not_1_out, not_2_out, not_4_out, Cond[3], Cond[2], not_8_out);
  and and_8 (and_8_out, not_2_out, not_3_out, ZNCV[0], not_6_out, Cond[1], Cond[0]);
  and and_9 (and_9_out, ZNCV[0], Cond[2], Cond[1], not_8_out);
  and and_10 (and_10_out, not_2_out, ZNCV[0], Cond[3], Cond[1], Cond[0]);
  and and_11 (and_11_out, ZNCV[1], not_5_out, not_6_out, Cond[1], not_8_out);
  and and_12 (and_12_out, not_1_out, ZNCV[1], Cond[3], not_6_out, not_7_out, not_8_out);
  and and_13 (and_13_out, ZNCV[2], not_5_out, Cond[2], not_7_out, not_8_out);
  and and_14 (and_14_out, ZNCV[2], not_4_out, Cond[3], Cond[1], Cond[0]);
  and and_15 (and_15_out, not_1_out, ZNCV[2], ZNCV[0], Cond[2], not_8_out);
  and and_16 (and_16_out, ZNCV[2], ZNCV[0], Cond[3], Cond[1], not_8_out);
  and and_17 (and_17_out, ZNCV[3], not_5_out, not_6_out, not_7_out, not_8_out);
  and and_18 (and_18_out, ZNCV[3], not_3_out, Cond[3], not_6_out, not_7_out, Cond[0]);
  and and_19 (and_19_out, ZNCV[3], not_2_out, ZNCV[0], Cond[3], Cond[2], Cond[0]);
  and and_20 (and_20_out, ZNCV[3], ZNCV[2], not_4_out, Cond[3], Cond[2], Cond[0]);
  or or_1 (Extra, and_1_out, and_2_out, and_3_out, and_4_out, and_5_out, and_6_out, and_7_out, and_8_out, and_9_out, and_10_out, and_11_out, and_12_out, and_13_out, and_14_out, and_15_out, and_16_out, and_17_out, and_18_out, and_19_out, and_20_out);
endmodule
